// Logisim project mine.circ as structural Verilog
module BCD_to_7_Segment_decoder (
  input  a,
  input  b,
  input  c,
  input  d,
  output A_2,
  output B_2,
  output C_2,
  output D_2,
  output E,
  output F,
  output G
);

  wire and_1_out, and_2_out, and_3_out, and_4_out, and_5_out, and_6_out, and_7_out, and_8_out, and_9_out,
       and_10_out, and_11_out, and_12_out, and_13_out, and_14_out, and_15_out, nand_1_out, not_1_out,
       not_2_out, not_3_out, not_4_out, not_5_out, not_6_out, not_7_out, not_8_out, not_9_out, not_10_out,
       not_11_out, not_12_out, not_13_out, not_14_out, not_15_out, not_16_out, not_17_out, not_18_out;

  not not_1 (not_1_out, b);
  not not_2 (not_2_out, d);
  not not_3 (not_3_out, b);
  not not_4 (not_4_out, d);
  not not_5 (not_5_out, c);
  not not_6 (not_6_out, d);
  not not_7 (not_7_out, b);
  not not_8 (not_8_out, b);
  not not_9 (not_9_out, d);
  not not_10 (not_10_out, d);
  not not_11 (not_11_out, c);
  not not_12 (not_12_out, c);
  not not_13 (not_13_out, d);
  not not_14 (not_14_out, c);
  not not_15 (not_15_out, d);
  not not_16 (not_16_out, b);
  and and_1 (and_1_out, not_1_out, not_2_out);
  and and_2 (and_2_out, b, d);
  nand nand_1 (nand_1_out, c, d);
  and and_3 (and_3_out, d, c);
  not not_17 (not_17_out, b);
  not not_18 (not_18_out, c);
  and and_4 (and_4_out, not_3_out, not_4_out);
  and and_5 (and_5_out, b, not_5_out, d);
  and and_6 (and_6_out, c, not_6_out);
  and and_7 (and_7_out, c, not_7_out);
  and and_8 (and_8_out, not_8_out, not_9_out);
  and and_9 (and_9_out, c, not_10_out);
  and and_10 (and_10_out, not_11_out, b);
  and and_11 (and_11_out, b, d);
  and and_12 (and_12_out, not_12_out, not_13_out);
  and and_13 (and_13_out, b, not_14_out);
  and and_14 (and_14_out, c, not_15_out);
  and and_15 (and_15_out, c, not_16_out);
  or or_1 (A_2, and_1_out, and_2_out, a, c);
  or or_2 (B_2, nand_1_out, and_3_out, not_17_out);
  or or_3 (C_2, d, not_18_out, b);
  or or_4 (D_2, and_4_out, and_5_out, a, and_6_out, and_7_out);
  or or_5 (E, and_8_out, and_9_out);
  or or_6 (F, and_10_out, a, and_11_out, and_12_out);
  or or_7 (G, a, and_13_out, and_14_out, and_15_out);
endmodule
